# Fritzing sketch CircuitofreeRTOS (saved by Fritzing 0.9.3b)
breadboards: 1

parts:
  Componente2 = Arduino Nano (Rev3.0)
  LED1 = LED - 3mm [color="Red (633nm)" package="3 mm [THT]"]  # not connected
  R1 = Resistor [tolerance=±5% resistance=220 package="1206 [SMD]"]
  U1 = POT [package=pot_alpha_rv16af-20]
  R2 = Resistor [tolerance=±5% resistance=220 package="1206 [SMD]"]
  LCD1 = LCD screen
  LCM1602_IIC2 = LCM1602 IIC [part_number="LCM1602 IIC" chip_label="LCM1602 IIC" package="DIP (Dual Inline) [THT]"]

nets:
  GND: Componente2.GND, R2.Pin_1, LCM1602_IIC2.GND
  N1: Componente2.D2, R1.Pin_1
  5V: Componente2.5V, LCM1602_IIC2.VCC
  N2: Componente2.A5, LCM1602_IIC2.SCL
  N3: Componente2.A4, LCM1602_IIC2.SDA
  N4: Componente2.A0, U1.S, R2.Pin_0
  VDD: LCD1.VDD, LCM1602_IIC2.VDD
  N5: LCD1.V0, LCM1602_IIC2.V0
  N6: LCD1.RS, LCM1602_IIC2.RS
  N7: LCD1.R/W, LCM1602_IIC2.RW
  N8: LCD1.E, LCM1602_IIC2.E
  N9: LCD1.DB0, LCM1602_IIC2.D0
  N10: LCD1.DB1, LCM1602_IIC2.D1
  N11: LCD1.DB2, LCM1602_IIC2.D2
  N12: LCD1.DB3, LCM1602_IIC2.D3
  N13: LCD1.DB4, LCM1602_IIC2.D4
  N14: LCD1.DB5, LCM1602_IIC2.D5
  N15: LCD1.DB6, LCM1602_IIC2.D6
  N16: LCD1.DB7, LCM1602_IIC2.D7
  N17: LCD1.LED+, LCM1602_IIC2.A
  N18: LCD1.LED-, LCM1602_IIC2.K
  N19: LCM1602_IIC2.LED_A, LCM1602_IIC2.LED_B

custom parts:
  LCM1602 IIC: I2C-Module to use a 1602 or 2004 LCD on with the wire.h libory Serial LCD Modul

// code stored in the sketch: free1.ino
#include <LiquidCrystal.h>
#include <Arduino_FreeRTOS.h>
#include <queue.h>
#include <task.h>
#include <semphr.h>
#include <Wire.h>
#include <LiquidCrystal_I2C.h>
 
/* defines - LCD */
#define LCD_16X2_CLEAN_LINE               "                "
#define LCD_16X2_I2C_ADDRESS             0x27
#define LCD_16X2_COLS                      16
#define LCD_16X2_ROWS                      2
 
/* defines - LED */
#define LED_PIN                      12
#define LED_THRESHOLD                3.58 /* V
 
/* defines - ADC */
#define ADC_MAX                      1023.0
#define MAX_VOLTAGE_ADC              5.0

/* #define portCHAR    char*/
 
/* tasks */
void task_breathing_light( void *pvParameters );
void task_serial( void *pvParameters );
void task_lcd( void *pvParameters );
void task_sensor( void *pvParameters );
void task_led( void *pvParameters );
 
/* Variaveis relacionadas ao LCD */
LiquidCrystal_I2C lcd(LCD_16X2_I2C_ADDRESS,
                      LCD_16X2_COLS,
                      LCD_16X2_ROWS);
 
/* filas (queues) */
QueueHandle_t xQueue_LCD, xQueue_LED;
 
/* semaforos utilizados */
SemaphoreHandle_t xSerial_semaphore;
 
void setup() {
  
  /* Inicializa serial (baudrate 9600) */
  Serial.begin(9600);
 
  /* Inicializa o LCD, liga o backlight e limpa o LCD */
  lcd.init();
  lcd.backlight();
  lcd.clear();
 
  /* Inicializa e configura GPIO do LED */
  pinMode(LED_PIN, OUTPUT);
  digitalWrite(LED_PIN, LOW);
  
  while (!Serial) {
    ; /* Somente vai em frente quando a serial estiver pronta para funcionar */
  }
 
  /* Criação das filas (queues) */
  xQueue_LCD = xQueueCreate( 1, sizeof( float ) );
  xQueue_LED = xQueueCreate( 1, sizeof( float ) );
 
  /* Criação dos semaforos */
  xSerial_semaphore = xSemaphoreCreateMutex();
 
  if (xSerial_semaphore == NULL)
  {
  Serial.println("Erro: nao e possivel criar o semaforo");
  while(1); /* Sem semaforo o funcionamento esta comprometido. Nada mais deve ser feito. */
  }
  
  /* Criação das tarefas */
  xTaskCreate(
    task_sensor                   /* Funcao a qual esta implementado o que a tarefa deve fazer */
    ,  (const portCHAR *)"sensor"   /* Nome (para fins de debug, se necessário) */
    ,  128                          /* Tamanho da stack (em words) reservada para essa tarefa */
    ,  NULL                       /* Parametros passados (nesse caso, não há) */
    ,  3                            /* Prioridade */
    ,  NULL );                      /* Handle da tarefa, opcional (nesse caso, não há) */
 
  xTaskCreate(
    task_lcd
    ,  (const portCHAR *) "L  CD"
    ,  156  
    ,  NULL
    ,  2
    ,  NULL );
 
 
  xTaskCreate(
    task_led
    ,  (const portCHAR *)"LED"
    ,  128  
    ,  NULL
    ,  1  
    ,  NULL );
 
  /* A partir deste momento, o scheduler de tarefas entra em ação e as tarefas executam */
}
 
void loop()
{
  /* Tudo é executado nas tarefas. Há nada a ser feito aqui. */
}
 
/* --------------------------------------------------*/
/* ---------------------- Tarefas -------------------*/
/* --------------------------------------------------*/
 
void task_sensor( void *pvParameters )
{
    (void) pvParameters;
    int adc_read=0;
    UBaseType_t uxHighWaterMark;
    float voltage = 0.0;
    
    while(1)
    {  
        adc_read = analogRead(0);
        voltage = ((float)adc_read/ADC_MAX)*MAX_VOLTAGE_ADC;
        
        /* Envia tensão lida em A0 para as tarefas a partir de filas */
        xQueueOverwrite(xQueue_LCD, (void *)&voltage);
        xQueueOverwrite(xQueue_LED, (void *)&voltage);
        
        /* Espera um segundo */
        vTaskDelay( 1000 / portTICK_PERIOD_MS );
 
        /* Para fins de teste de ocupação de stack, printa na serial o high water mark */
        xSemaphoreTake(xSerial_semaphore, portMAX_DELAY );
        
        uxHighWaterMark = uxTaskGetStackHighWaterMark( NULL );
        Serial.print("task_sensor high water mark (words): ");
        Serial.println(uxHighWaterMark);
        Serial.println("---");
        xSemaphoreGive(xSerial_semaphore);
    }
}
 
void task_lcd( void *pvParameters )
{
    (void) pvParameters;
    float voltage_rcv = 0.0;
    UBaseType_t uxHighWaterMark;
 
    while(1)
    {        
        /* Espera até algo ser recebido na queue */
        xQueueReceive(xQueue_LCD, (void *)&voltage_rcv, portMAX_DELAY);
        
        /* Uma vez recebida a informação na queue, a escreve no display LCD */
        lcd.setCursor(0,0);
        lcd.print("Voltage: ");
        lcd.setCursor(0,1);
        lcd.print(LCD_16X2_CLEAN_LINE);
        lcd.setCursor(0,1);
        lcd.print(voltage_rcv);
        lcd.setCursor(15,1);
        lcd.print("V");
 
        /* Para fins de teste de ocupação de stack, printa na serial o high water mark */
        xSemaphoreTake(xSerial_semaphore, portMAX_DELAY );
        
        uxHighWaterMark = uxTaskGetStackHighWaterMark( NULL );
        Serial.print("task_lcd high water mark (words): ");
        Serial.println(uxHighWaterMark);
        Serial.println("---");
        xSemaphoreGive(xSerial_semaphore);
    }  
}
 
void task_led( void *pvParameters )
{
    (void) pvParameters;
    float voltage_rcv = 0.0;
    UBaseType_t uxHighWaterMark;
 
    while(1)
    {    
        /* Espera até algo ser recebido na queue */
        xQueueReceive(xQueue_LED, (void *)&voltage_rcv, portMAX_DELAY);  
 
        /* Uma vez recebida a informação na queue, verifica se o LED deve acender ou não */
        if (voltage_rcv > LED_THRESHOLD)
            digitalWrite(LED_PIN, HIGH);  
        else
            digitalWrite(LED_PIN, LOW);  
 
        /* Para fins de teste de ocupação de stack, printa na serial o high water mark */
        xSemaphoreTake(xSerial_semaphore, portMAX_DELAY );
        
        uxHighWaterMark = uxTaskGetStackHighWaterMark( NULL );
        Serial.print("task_led high water mark (words): ");
        Serial.println(uxHighWaterMark);
        Serial.println("---");    
        xSemaphoreGive(xSerial_semaphore);
    }  
}
